# Fritzing sketch esp32s_adaptador (saved by Fritzing 0.9.3b)
circuit board: 6.5cm x 4.5cm
breadboards: 1

parts:
  Micro_USB = ESP32S-HiLetgo [part_number=ESP32S-HiLetgo]
  S1 = Tactile Switch Buttons - 12mm Square [package=tactile-pth-12mm]
  J2 = Camdenboss CTB0158-2 [part_number=CTB0158-2 package=THT]
  J4 = female pin header, 19 pins [form="♀ (female)"]
  J5 = female pin header, 19 pins [form="♀ (female)"]
  J6 = female pin header, 10 pins [form="♀ (female)"]
  J7 = male pin header, 9 pins [form="♂ (male)"]
  J8 = female pin header, 19 pins [form="♀ (female)"]
  J9 = female pin header, 19 pins [form="♀ (female)"]
  J3 = male pin header, 19 pins [form="♂ (male)"]
  J10 = male pin header, 19 pins [form="♂ (male)"]
  J11 = female pin header, 10 pins [form="♀ (female)"]
  J12 = male pin header, 9 pins [form="♂ (male)"]
  J13 = male pin header, 3 pins [form="♂ (male)"]
  J14 = male pin header, 3 pins [form="♂ (male)"]

nets (from the pcb view):
  N1: Micro_USB.3.3, J4.pin1, J5.pin1, J3.pin1
  N2: Micro_USB.EN, J4.pin2, J5.pin2, J3.pin2
  N3: Micro_USB.GPIO36, J4.pin3, J5.pin3, J3.pin3
  N4: Micro_USB.GPIO39, J4.pin4, J5.pin4, J3.pin4
  N5: Micro_USB.GPIO34, J4.pin5, J5.pin5, J3.pin5
  N6: Micro_USB.GPIO35, J4.pin6, J5.pin6, J3.pin6
  N7: Micro_USB.GPIO32, J4.pin7, J5.pin7, J3.pin7
  N8: Micro_USB.GPIO33, J4.pin8, J5.pin8, J3.pin8
  N9: Micro_USB.GPIO25, J4.pin9, J5.pin9, J3.pin9
  N10: Micro_USB.GPIO26, J4.pin10, J5.pin10, J3.pin10
  N11: Micro_USB.GPIO27, J4.pin11, J5.pin11, J3.pin11
  N12: Micro_USB.GPIO14, J4.pin12, J5.pin12, J3.pin12
  N13: Micro_USB.GPIO12, J4.pin13, J5.pin13, J3.pin13
  N14: Micro_USB.GND, J4.pin14, J5.pin14, J8.pin1, J8.pin7, J9.pin1, J9.pin7, J3.pin14, J10.pin1, J10.pin7, J14.pin1
  N15: Micro_USB.GPIO13, J4.pin15, J5.pin15, J3.pin15
  N16: Micro_USB.GPIO9, J4.pin16, J5.pin16, J3.pin16
  N17: Micro_USB.GPIO10, J4.pin17, J5.pin17, J3.pin17
  N18: Micro_USB.GPIO11, J4.pin18, J5.pin18, J3.pin18
  N19: Micro_USB.VIN, J4.pin19, J5.pin19, J3.pin19
  N20: Micro_USB.GPIO6, J8.pin19, J9.pin19, J10.pin19
  N21: Micro_USB.GPIO7, J8.pin18, J9.pin18, J10.pin18
  N22: Micro_USB.GPIO8, J8.pin17, J9.pin17, J10.pin17
  N23: Micro_USB.GPIO15, J8.pin16, J9.pin16, J10.pin16
  N24: Micro_USB.GPIO2, J8.pin15, J9.pin15, J10.pin15
  N25: Micro_USB.GPIO0, J8.pin14, J9.pin14, J10.pin14
  N26: Micro_USB.GPIO4, J8.pin13, J9.pin13, J10.pin13
  N27: Micro_USB.GPIO16, J8.pin12, J9.pin12, J10.pin12
  N28: Micro_USB.GPIO17, J8.pin11, J9.pin11, J10.pin11
  N29: Micro_USB.GPIO5, J8.pin10, J9.pin10, J10.pin10
  N30: Micro_USB.GPIO18, J8.pin9, J9.pin9, J10.pin9
  N31: Micro_USB.GPIO19, J8.pin8, J9.pin8, J10.pin8
  N32: Micro_USB.GPIO21, J8.pin6, J9.pin6, J10.pin6
  N33: Micro_USB.GPIO3, J8.pin5, J9.pin5, J10.pin5
  N34: Micro_USB.GPIO1, J8.pin4, J9.pin4, J10.pin4
  N35: Micro_USB.GPIO22, J8.pin3, J9.pin3, J10.pin3
  N36: Micro_USB.GPIO23, J8.pin2, J9.pin2, J10.pin2
  N37: S1.1, S1.3, J13.pin3
  N38: S1.2, S1.4, J13.pin1
  N39: J2.pin1, J11.pin1, J11.pin2, J11.pin3, J11.pin4, J11.pin5, J11.pin6, J11.pin7, J11.pin8, J11.pin9, J11.pin10, J12.pin1, J12.pin2, J12.pin3, J12.pin4, J12.pin5, J12.pin6, J12.pin7, J12.pin8, J12.pin9
  N40: J2.pin2, J6.pin1, J6.pin2, J6.pin3, J6.pin4, J6.pin5, J6.pin6, J6.pin7, J6.pin8, J6.pin9, J6.pin10, J7.pin1, J7.pin2, J7.pin3, J7.pin4, J7.pin5, J7.pin6, J7.pin7, J7.pin8, J7.pin9, J14.pin2

custom parts:
  ESP32S-HiLetgo: HiLetgo ESP-WROOM-32 ESP32 ESP-32S Development Board 2.4GHz Dual-Mode WiFi + Bluetooth Dual Cores Microcontroller The ESP32 integrated with Antenna switches, RF Balun, power amplifiers, low-noise amplifiers, filters, and management modules, and the entire solution occupies the least area of PCB. 2.4 GHz Wi-Fi plus Bluetooth dual-mode chip, with TSMC Ultra-low power consumption 40nm technology,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
  Tactile Switch Buttons - 12mm Square: Medium-sized clicky momentary switches are standard input "buttons" on electronic projects. These work best in a PCB but can be used on a solderless breadboard as shown in this tutorial. The pins are normally open (disconnected) and when the button is pressed they are momentarily closed. They come in a pack of 10, they're pretty handy so you'll want to keep them around. You can find an EAGLE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
